// Digital circuit main.dig as structural Verilog
module main (
  input  in_1,
  input  [7:0] in_2,
  input  [7:0] in_3,
  input  clk,
  output [7:0] out_4
);

  memory_256x8 #(.applicationType("IVERILOG"), .CodeFile("/home/kaldwin/Development/Projects/the_electronics_project_misc/src/memory_256x8.v")) u_memory_256x8 (
    .clk(clk), .write(in_1), .address(in_2), .data_in(in_3), .data_out(out_4));

  // Notes on the sheet:
  //   clk: Hz: 50
endmodule
